# Fritzing sketch fz_numenu breadboard (saved by Fritzing 0.9.3b)
breadboards: 1

parts:
  Part2 = Arduino Uno (Rev3) - ICSP
  LCD1 = LCD screen
  R1 = Resistor [tolerance=±5% resistance=220 package="2010 [SMD]"]
  R2 = Trimmer Potentiometer [maximum_resistance=10kΩ package=THT]
  S1 = Momentary Switch [package=ksa_sealed_tac_switch]
  U1 = ESP8266 WiFi Module [part_number=ESP8266]

nets:
  GND: Part2.GND, LCD1.VSS, LCD1.R/W, LCD1.LED-, R2.leg1, S1.3, U1.GPIO_0, U1.GND
  N1: Part2.D8, LCD1.DB7
  N2: Part2.D9_PWM, LCD1.DB6
  N3: Part2.D10_PWM/SS, LCD1.DB5
  N4: Part2.D11_PWM/MOSI, LCD1.DB4
  N5: Part2.D12/MISO, LCD1.E
  N6: Part2.D13/SCK, LCD1.RS
  N7: Part2.D0/RX, U1.TXD
  N8: Part2.D1/TX, U1.RXD
  N9: Part2.D7, S1.1
  3V3: Part2.3V3, U1.VCC, U1.CH_PD
  5V: Part2.5V, LCD1.VDD, R1.Pin_1, R2.leg2
  N10: LCD1.V0, R2.wiper
  N11: LCD1.LED+, R1.Pin_0

custom parts:
  ESP8266 WiFi Module: Generic WiFi Module based on the ESP8266 with onboard PCB antenna and UART communications
